// Logisim project Rams.circ as structural Verilog: 5 circuits, main circuit main
module main (
  input  [1:0] in_1,
  input  in_2,
  input  [15:0] FORCE_WRITE,
  input  in_4,
  input  [1:0] A_REG,
  input  [1:0] B_REG,
  input  [1:0] WRITE_REG,
  input  WRITE_DATA,
  input  CLK,
  output [15:0] out_10
);

  wire alu_16_bits_1_overflow, alu_16_bits_1_zero;
  wire [15:0] registerfile_1_out_a, registerfile_1_out_b;

  RegisterFile registerfile_1 (
    .DATA(out_10), .CLK(CLK), .OUT_A(registerfile_1_out_a), .OUT_B(registerfile_1_out_b),
    .WRITE_DATA(WRITE_DATA), .in_5(WRITE_REG), .REG_A(A_REG), .REG_B(B_REG));
  ALU_16_bits alu_16_bits_1 (
    .a(registerfile_1_out_a), .b(registerfile_1_out_b), .Operation(in_1), .Ainvert(in_2), .Bnegate(in_4),
    .Overflow(alu_16_bits_1_overflow), .Result(out_10), .Zero(alu_16_bits_1_zero));
  LED led_1 (.in(alu_16_bits_1_overflow));
  LED led_2 (.in(alu_16_bits_1_zero));
endmodule

// ALU
module ALU_1_bit (
  input  a,
  input  Ainvert,
  input  b,
  input  CarryIn,
  input  [1:0] Operation,
  input  Binvert,
  input  Less,
  output Set,
  output Result,
  output CarryOut
);

  wire and_1_out, multiplexer_1_out, multiplexer_2_out, not_1_out, not_2_out, or_1_out;

  not not_1 (not_1_out, a);
  not not_2 (not_2_out, b);
  Multiplexer multiplexer_1 (.in0(a), .in1(not_1_out), .out(multiplexer_1_out), .sel(Ainvert));  // open: en
  Multiplexer multiplexer_2 (.in0(b), .in1(not_2_out), .out(multiplexer_2_out), .sel(Binvert));  // open: en
  and and_1 (and_1_out, multiplexer_1_out, multiplexer_2_out);
  or or_1 (or_1_out, multiplexer_1_out, multiplexer_2_out);
  Adder #(.width(1)) adder_1 (.a(multiplexer_1_out), .b(multiplexer_2_out), .out(Set), .cin(CarryIn), .cout(CarryOut));
  Multiplexer #(.select(2)) multiplexer_3 (
    .in0(and_1_out), .in1(or_1_out), .in2(Set), .in3(Less), .out(Result), .sel(Operation));  // open: en
endmodule

module ALU_16_bits (
  input  Ainvert,
  input  Bnegate,
  input  [1:0] Operation,
  input  [15:0] a,
  input  [15:0] b,
  output [15:0] Result,
  output Zero,
  output Overflow
);

  wire alu_1_bit_1_carryout, alu_1_bit_2_carryout, alu_1_bit_3_carryout, alu_1_bit_4_carryout,
       alu_1_bit_5_carryout, alu_1_bit_6_carryout, alu_1_bit_7_carryout, alu_1_bit_8_carryout,
       alu_1_bit_9_carryout, alu_1_bit_10_carryout, alu_1_bit_11_carryout, alu_1_bit_12_carryout,
       alu_1_bit_13_carryout, alu_1_bit_14_carryout, alu_1_bit_15_carryout, alu_1_bit_16_set, or_1_out;

  ALU_1_bit alu_1_bit_1 (
    .a(a[0]), .b(b[0]), .Less(alu_1_bit_16_set), .Ainvert(Ainvert), .Result(Result[0]), .CarryIn(Bnegate),
    .Operation(Operation), .Binvert(Bnegate), .CarryOut(alu_1_bit_1_carryout));  // open: Set
  ALU_1_bit alu_1_bit_2 (
    .a(a[1]), .b(b[1]), .Less(1'b0), .Ainvert(Ainvert), .Result(Result[1]), .CarryIn(alu_1_bit_1_carryout),
    .Operation(Operation), .Binvert(Bnegate), .CarryOut(alu_1_bit_2_carryout));  // open: Set
  ALU_1_bit alu_1_bit_3 (
    .a(a[2]), .b(b[2]), .Less(1'b0), .Ainvert(Ainvert), .Result(Result[2]), .CarryIn(alu_1_bit_2_carryout),
    .Operation(Operation), .Binvert(Bnegate), .CarryOut(alu_1_bit_3_carryout));  // open: Set
  ALU_1_bit alu_1_bit_4 (
    .a(a[3]), .b(b[3]), .Less(1'b0), .Ainvert(Ainvert), .Result(Result[3]), .CarryIn(alu_1_bit_3_carryout),
    .Operation(Operation), .Binvert(Bnegate), .CarryOut(alu_1_bit_4_carryout));  // open: Set
  ALU_1_bit alu_1_bit_5 (
    .a(a[4]), .b(b[4]), .Less(1'b0), .Ainvert(Ainvert), .Result(Result[4]), .CarryIn(alu_1_bit_4_carryout),
    .Operation(Operation), .Binvert(Bnegate), .CarryOut(alu_1_bit_5_carryout));  // open: Set
  ALU_1_bit alu_1_bit_6 (
    .a(a[5]), .b(b[5]), .Less(1'b0), .Ainvert(Ainvert), .Result(Result[5]), .CarryIn(alu_1_bit_5_carryout),
    .Operation(Operation), .Binvert(Bnegate), .CarryOut(alu_1_bit_6_carryout));  // open: Set
  ALU_1_bit alu_1_bit_7 (
    .a(a[6]), .b(b[6]), .Less(1'b0), .Ainvert(Ainvert), .Result(Result[6]), .CarryIn(alu_1_bit_6_carryout),
    .Operation(Operation), .Binvert(Bnegate), .CarryOut(alu_1_bit_7_carryout));  // open: Set
  ALU_1_bit alu_1_bit_8 (
    .a(a[7]), .b(a[7]), .Less(1'b0), .Ainvert(Ainvert), .Result(Result[7]), .CarryIn(alu_1_bit_7_carryout),
    .Operation(Operation), .Binvert(Bnegate), .CarryOut(alu_1_bit_8_carryout));  // open: Set
  ALU_1_bit alu_1_bit_9 (
    .a(a[8]), .b(b[8]), .Less(1'b0), .Ainvert(Ainvert), .Result(Result[8]), .CarryIn(alu_1_bit_8_carryout),
    .Operation(Operation), .Binvert(Bnegate), .CarryOut(alu_1_bit_9_carryout));  // open: Set
  ALU_1_bit alu_1_bit_10 (
    .a(a[9]), .b(b[9]), .Less(1'b0), .Ainvert(Ainvert), .Result(Result[9]), .CarryIn(alu_1_bit_9_carryout),
    .Operation(Operation), .Binvert(Bnegate), .CarryOut(alu_1_bit_10_carryout));  // open: Set
  ALU_1_bit alu_1_bit_11 (
    .a(a[10]), .b(b[10]), .Less(1'b0), .Ainvert(Ainvert), .Result(Result[10]),
    .CarryIn(alu_1_bit_10_carryout), .Operation(Operation), .Binvert(Bnegate),
    .CarryOut(alu_1_bit_11_carryout));  // open: Set
  ALU_1_bit alu_1_bit_12 (
    .a(a[11]), .b(b[11]), .Less(1'b0), .Ainvert(Ainvert), .Result(Result[11]),
    .CarryIn(alu_1_bit_11_carryout), .Operation(Operation), .Binvert(Bnegate),
    .CarryOut(alu_1_bit_12_carryout));  // open: Set
  ALU_1_bit alu_1_bit_13 (
    .a(a[12]), .b(b[12]), .Less(1'b0), .Ainvert(Ainvert), .Result(Result[12]),
    .CarryIn(alu_1_bit_12_carryout), .Operation(Operation), .Binvert(Bnegate),
    .CarryOut(alu_1_bit_13_carryout));  // open: Set
  ALU_1_bit alu_1_bit_14 (
    .a(a[13]), .b(b[13]), .Less(1'b0), .Ainvert(Ainvert), .Result(Result[13]),
    .CarryIn(alu_1_bit_13_carryout), .Operation(Operation), .Binvert(Bnegate),
    .CarryOut(alu_1_bit_14_carryout));  // open: Set
  ALU_1_bit alu_1_bit_15 (
    .a(a[14]), .b(b[14]), .Less(1'b0), .Ainvert(Ainvert), .Result(Result[14]),
    .CarryIn(alu_1_bit_14_carryout), .Operation(Operation), .Binvert(Bnegate),
    .CarryOut(alu_1_bit_15_carryout));  // open: Set
  ALU_1_bit alu_1_bit_16 (
    .a(a[15]), .b(b[15]), .Less(1'b0), .Ainvert(Ainvert), .Result(Result[15]),
    .CarryIn(alu_1_bit_15_carryout), .Operation(Operation), .Binvert(Bnegate), .Set(alu_1_bit_16_set),
    .CarryOut(Overflow));
  or or_1 (or_1_out, Result[0], Result[1], Result[2], Result[3], Result[4], Result[5], Result[6], Result[7], Result[8], Result[9], Result[10], Result[11], Result[12], Result[13], Result[14], Result[15]);
  not not_1 (Zero, or_1_out);

  assign b[7] = a[7];
endmodule

module RegisterFile (
  input  [15:0] DATA,
  input  CLK,
  input  [1:0] REG_A,
  input  WRITE_DATA,
  input  [1:0] in_5,
  input  [1:0] REG_B,
  output [15:0] OUT_A,
  output [15:0] OUT_B
);

  wire demultiplexer_1_out0, demultiplexer_1_out1, demultiplexer_1_out2, demultiplexer_1_out3;
  wire [15:0] register_1_q, register_2_q, register_3_q, register_4_q;

  Demultiplexer #(.select(2)) demultiplexer_1 (
    .out0(demultiplexer_1_out0), .out1(demultiplexer_1_out1), .out2(demultiplexer_1_out2),
    .out3(demultiplexer_1_out3), .in(CLK), .sel(in_5), .en(WRITE_DATA));
  Register #(.width(16)) register_1 (.D(DATA), .Q(register_1_q), .clk(demultiplexer_1_out0));  // open: en, clr
  Register #(.width(16)) register_2 (.D(DATA), .Q(register_2_q), .clk(demultiplexer_1_out1));  // open: en, clr
  Register #(.width(16)) register_3 (.D(DATA), .Q(register_3_q), .clk(demultiplexer_1_out2));  // open: en, clr
  Register #(.width(16)) register_4 (.D(DATA), .Q(register_4_q), .clk(demultiplexer_1_out3));  // open: en, clr
  Multiplexer #(.select(2), .width(16)) multiplexer_1 (
    .in0(register_1_q), .in1(register_2_q), .in2(register_3_q), .in3(register_4_q), .out(OUT_A), .sel(REG_A));  // open: en
  Multiplexer #(.select(2), .width(16)) multiplexer_2 (
    .in0(register_1_q), .in1(register_2_q), .in2(register_3_q), .in3(register_4_q), .out(OUT_B), .sel(REG_B));  // open: en
endmodule

module k (
  input  in_1,
  input  in_2,
  input  in_3,
  input  in_4,
  input  in_5,
  input  in_6,
  output RegDest,
  output Branch,
  output MemRead,
  output MemToReg,
  output ALUOp0,
  output ALUOp1,
  output MemWrite,
  output ALUSrc,
  output RegWrite,
  output Jump
);
endmodule
